// Logisim project 01-water.circ as structural Verilog: 1 circuit, main circuit main
module main (
  input  F,
  input  M,
  input  C,
  input  H,
  input  P,
  output R,
  output G,
  output B2,
  output B1
);

  wire and_1_out, and_2_out, and_3_out, or_1_out, or_2_out, or_3_out, or_4_out;

  or or_1 (or_1_out, M, F);
  and and_1 (and_1_out, C, P);
  or or_2 (or_2_out, F, M);
  or or_3 (or_3_out, C, H, P);
  or or_4 (or_4_out, H, P);
  and and_2 (and_2_out, M, P);
  and and_3 (and_3_out, M, F);
  and and_4 (B2, or_1_out, and_1_out);
  or or_5 (B1, and_2_out, and_3_out);
  and and_5 (R, M, or_3_out);
  and and_6 (G, or_2_out, or_4_out);
endmodule
