// Logisim project 01-water2.circ as structural Verilog: 1 circuit, main circuit main
module main (
  input  H,
  input  C,
  input  P,
  input  M,
  input  F,
  output G,
  output R,
  output B,
  output B2
);

  wire and_1_out, and_2_out, and_3_out, or_1_out, or_3_out;

  or or_1 (or_1_out, M, F);
  or or_2 (G, H, C);
  and and_1 (and_1_out, C, P);
  and and_2 (and_2_out, P, M);
  or or_3 (or_3_out, G, P);
  and and_3 (and_3_out, C, M);
  and and_4 (B2, and_1_out, or_1_out);
  and and_5 (R, or_3_out, M);
  or or_4 (B, and_2_out, and_3_out);
endmodule
