// Logisim project 02-car.circ as structural Verilog: 1 circuit, main circuit main
module main (
  input  K,
  input  C,
  input  S,
  output B,
  output E
);

  wire nand_1_out;

  nand nand_1 (nand_1_out, C, S);
  and and_1 (B, K, nand_1_out);
  and and_2 (E, K, C, S);
endmodule
