// Logisim project 02-hw.circ as structural Verilog: 1 circuit, main circuit main
module main (
  input  A,
  input  B,
  input  C,
  input  D,
  output out_5
);

  wire nand_1_out, or_1_out;

  or or_1 (or_1_out, B, C);
  nand nand_1 (nand_1_out, or_1_out, D);
  and and_1 (out_5, A, nand_1_out);
endmodule
