// Logisim project 03- Hw00.circ as structural Verilog: 1 circuit, main circuit main
module main (
  input  B,
  input  C,
  output A,
  output B_2,
  output C_2,
  output D,
  output E,
  output F,
  output G
);

  wire not_1_out, not_2_out;

  not not_1 (not_1_out, C);
  not not_2 (not_2_out, B);
  and and_1 (B_2, not_1_out, B);
  and and_2 (C_2, not_2_out, B);
  or or_1 (A, C, B);
  _7_Segment_Display u_7_segment_display_1 (.g(B), .f(A), .a(A), .b(B_2), .e(A), .d(C), .c(C_2));  // open: dp

  assign D = C;
  assign E = A;
  assign F = A;
  assign G = B;
endmodule
