// Logisim project 03-HwCPE.circ as structural Verilog: 2 circuits, main circuit main
module main (
  input  B,
  input  C,
  input  B_2,
  input  C_2,
  input  B_3,
  input  C_3
);

  wire c_1_a, c_1_b_2, c_1_c_2, c_1_d, c_1_e, c_1_f, c_1_g, c_2_a, c_2_b_2, c_2_c_2, c_2_d, c_2_e, c_2_f,
       c_2_g, c_3_a, c_3_b_2, c_3_c_2, c_3_d, c_3_e, c_3_f, c_3_g;

  C c_1 (.B(B), .C(C), .A(c_1_a), .B_2(c_1_b_2), .C_2(c_1_c_2), .D(c_1_d), .E(c_1_e), .F(c_1_f), .G(c_1_g));
  C u_c_2 (.B(B_2), .C(C_2), .A(c_2_a), .B_2(c_2_b_2), .C_2(c_2_c_2), .D(c_2_d), .E(c_2_e), .F(c_2_f), .G(c_2_g));
  C u_c_3 (.B(B_3), .C(C_3), .A(c_3_a), .B_2(c_3_b_2), .C_2(c_3_c_2), .D(c_3_d), .E(c_3_e), .F(c_3_f), .G(c_3_g));
  _7_Segment_Display u_7_segment_display_1 (
    .g(c_1_g), .f(c_1_f), .a(c_1_a), .b(c_1_b_2), .e(c_1_e), .d(c_1_d), .c(c_1_c_2));  // open: dp
  _7_Segment_Display u_7_segment_display_2 (
    .g(c_2_g), .f(c_2_f), .a(c_2_a), .b(c_2_b_2), .e(c_2_e), .d(c_2_d), .c(c_2_c_2));  // open: dp
  _7_Segment_Display u_7_segment_display_3 (
    .g(c_3_g), .f(c_3_f), .a(c_3_a), .b(c_3_b_2), .e(c_3_e), .d(c_3_d), .c(c_3_c_2));  // open: dp
endmodule

module C (
  input  B,
  input  C,
  output A,
  output B_2,
  output C_2,
  output D,
  output E,
  output F,
  output G
);

  wire not_1_out, not_2_out;

  not not_1 (not_1_out, C);
  not not_2 (not_2_out, B);
  and and_1 (B_2, not_1_out, B);
  and and_2 (C_2, not_2_out, B);
  or or_1 (A, C, B);

  assign D = C;
  assign E = A;
  assign F = A;
  assign G = B;
endmodule
