// Logisim project 03-Lab.circ as structural Verilog: 1 circuit, main circuit main
module main (
  input  A,
  input  B,
  input  C,
  output L4,
  output L5,
  output L2,
  output L1,
  output L3
);

  wire and_1_out, or_2_out;

  or or_1 (L2, A, B);
  or or_2 (or_2_out, B, C);
  and and_1 (and_1_out, B, C);
  or or_3 (L1, A, or_2_out);
  and and_2 (L5, A, or_2_out);
  or or_4 (L3, A, and_1_out);

  assign L4 = A;
endmodule
