// Logisim project 04-HW01.circ as structural Verilog: 3 circuits, main circuit main
module main (
  input  A,
  input  B,
  input  C,
  input  D,
  output out_5
);

  wire not_1_out, parity_odd_1_out_5, parity_odd_2_out_5;

  parity_odd parity_odd_1 (.A(A), .B(B), .C(C), .D(D), .out_5(parity_odd_1_out_5));
  not not_1 (not_1_out, A);
  parity_odd parity_odd_2 (.A(not_1_out), .B(B), .C(C), .D(D), .out_5(parity_odd_2_out_5));
  xnor xnor_1 (out_5, parity_odd_1_out_5, parity_odd_2_out_5);

  // Notes on the sheet:
  //   0 = Error
endmodule

module parity_odd (
  input  A,
  input  B,
  input  C,
  input  D,
  output out_5
);

  wire xnor_1_out, xnor_2_out;

  xnor xnor_1 (xnor_1_out, A, B);
  xnor xnor_2 (xnor_2_out, C, D);
  xnor xnor_3 (out_5, xnor_1_out, xnor_2_out);
endmodule

module parity_even (
  input  in_1,
  input  in_2,
  input  in_3,
  input  in_4,
  output out_5
);

  wire xor_1_out, xor_2_out;

  xor xor_1 (xor_1_out, in_1, in_2);
  xor xor_2 (xor_2_out, in_3, in_4);
  or or_1 (out_5, xor_1_out, xor_2_out);
endmodule
