// Logisim project 04-Lab.circ as structural Verilog: 1 circuit, main circuit main
module main (
  input  A,
  input  B
);

  wire and_1_out, and_2_out, and_3_out, and_4_out, not_1_out, not_2_out, not_3_out, or_1_out;

  not not_1 (not_1_out, A);
  not not_2 (not_2_out, B);
  and and_1 (and_1_out, 1'b0, not_2_out, not_1_out);
  and and_2 (and_2_out, 1'b1, B, not_1_out);
  and and_3 (and_3_out, 1'b1, not_2_out, A);
  and and_4 (and_4_out, 1'b0, B, A);
  or or_1 (or_1_out, and_1_out, and_2_out, and_3_out, and_4_out);
  LED led_1 (.in(or_1_out));
  LED led_2 (.in(not_3_out));
  not not_3 (not_3_out, or_1_out);
endmodule
