// Logisim project 05-HW.circ as structural Verilog: 1 circuit, main circuit main
module main (
  output A,
  output B,
  output out_3
);

  wire and_1_out, and_2_out, button_1_out, clock_1_out, nand_1_out, not_1_out, or_1_out;

  Button button_1 (.out(button_1_out));
  or or_1 (or_1_out, A, B);
  nand nand_1 (nand_1_out, A, B);
  not not_1 (not_1_out, or_1_out);
  and and_1 (and_1_out, or_1_out, nand_1_out, button_1_out);
  and and_2 (and_2_out, not_1_out, button_1_out);
  Clock clock_1 (.out(clock_1_out));
  D_Flip_Flop d_ff_1 (.clk(clock_1_out), .D(and_1_out), .Q(A));  // open: Qn, preset, en, reset
  D_Flip_Flop d_ff_2 (.clk(clock_1_out), .D(and_2_out), .Q(B));  // open: Qn, preset, en, reset

  assign out_3 = B;
endmodule
