// Logisim project 06-1.circ as structural Verilog: 1 circuit, main circuit main
module main (
  input  R,
  input  L,
  input  H,
  output _1,
  output _2,
  output _3,
  output _4,
  output _5,
  output _6
);

  wire _001_out, _010_out, _011_out, and_1_out, and_2_out, and_3_out, and_4_out, and_5_out, and_6_out,
       and_7_out, and_8_out, and_9_out, and_10_out, B_q, C_q, clock_1_out, not_1_out, not_2_out, or_1_out,
       or_2_out, or_3_out;

  or or_1 (or_1_out, R, L);
  not not_1 (not_1_out, C_q);
  and _001 (_001_out, or_1_out, C_q);
  and _010 (_010_out, or_1_out, not_1_out, B_q);
  not not_2 (not_2_out, _001_out);
  and and_1 (and_1_out, not_2_out, or_1_out);
  or or_2 (or_2_out, _010_out, _001_out);
  nand _011 (_011_out, C_q, B_q);
  and and_2 (and_2_out, _011_out, _010_out, or_1_out);
  and and_3 (and_3_out, _011_out, or_2_out);
  or or_3 (or_3_out, _010_out, and_2_out, and_1_out);
  Clock clock_1 (.out(clock_1_out));
  D_Flip_Flop B (.clk(clock_1_out), .D(and_3_out), .Q(B_q));  // open: Qn, preset, en, reset
  D_Flip_Flop C (.clk(clock_1_out), .D(or_3_out), .Q(C_q));  // open: Qn, preset, en, reset
  and and_4 (and_4_out, H, clock_1_out);
  and and_5 (and_5_out, L, B_q);
  and and_6 (and_6_out, L, C_q);
  and and_7 (and_7_out, C_q, R);
  and and_8 (and_8_out, B_q, R);
  and and_9 (and_9_out, and_5_out, and_6_out);
  or or_4 (_2, and_5_out, and_4_out);
  or or_5 (_3, and_5_out, and_4_out, and_6_out);
  or or_6 (_4, and_7_out, and_4_out, and_8_out);
  or or_7 (_5, and_8_out, and_4_out);
  and and_10 (and_10_out, and_7_out, and_8_out);
  or or_8 (_1, and_9_out, and_4_out);
  or or_9 (_6, and_10_out, and_4_out);
endmodule
