// Logisim project 06.circ as structural Verilog: 1 circuit, main circuit main
module main (
  input  R,
  input  L,
  input  H,
  output _1,
  output _2,
  output _3,
  output _4,
  output _5,
  output _6
);

  wire A_q, and_1_out, and_2_out, and_3_out, and_4_out, and_5_out, and_6_out, and_7_out, and_8_out,
       and_9_out, and_10_out, and_11_out, and_12_out, and_13_out, and_14_out, and_15_out, and_16_out,
       and_17_out, and_18_out, B_q, C_q, clock_1_out, nand_1_out, nand_2_out, not_1_out, not_2_out, or_1_out,
       or_2_out, or_3_out, or_4_out, or_5_out;

  and and_1 (and_1_out, L, B_q);
  and and_2 (and_2_out, L, C_q);
  not not_1 (not_1_out, C_q);
  or or_1 (or_1_out, and_1_out, and_2_out);
  and and_3 (and_3_out, not_1_out, L);
  or or_2 (or_2_out, and_1_out, and_3_out);
  nand nand_1 (nand_1_out, R, B_q);
  and and_4 (and_4_out, R, A_q);
  and and_5 (and_5_out, or_1_out, and_7_out);
  nand nand_2 (nand_2_out, B_q, C_q);
  and and_6 (and_6_out, A_q, R);
  and and_7 (and_7_out, nand_2_out, L);
  not not_2 (not_2_out, and_6_out);
  and and_8 (and_8_out, not_2_out, and_4_out);
  and and_9 (and_9_out, or_2_out, and_7_out);
  or or_3 (or_3_out, R, and_6_out);
  or or_4 (or_4_out, and_6_out, and_5_out);
  or or_5 (or_5_out, and_9_out, and_8_out);
  and and_10 (and_10_out, nand_1_out, or_3_out);
  and and_11 (and_11_out, nand_1_out, or_5_out);
  Clock clock_1 (.out(clock_1_out));
  D_Flip_Flop A (.clk(clock_1_out), .D(and_10_out), .Q(A_q));  // open: Qn, preset, en, reset
  D_Flip_Flop B (.clk(clock_1_out), .D(or_4_out), .Q(B_q));  // open: Qn, preset, en, reset
  D_Flip_Flop C (.clk(clock_1_out), .D(and_11_out), .Q(C_q));  // open: Qn, preset, en, reset
  and and_12 (and_12_out, L, B_q);
  and and_13 (and_13_out, L, C_q);
  and and_14 (and_14_out, A_q, R);
  and and_15 (and_15_out, C_q, R);
  and and_16 (and_16_out, B_q, R);
  and and_17 (and_17_out, clock_1_out, H);
  and and_18 (and_18_out, and_12_out, and_13_out);
  or or_6 (_1, and_18_out, and_17_out);
  or or_7 (_2, and_17_out, and_12_out);
  or or_8 (_3, and_12_out, and_17_out, and_13_out);
  or or_9 (_4, and_14_out, and_17_out);
  or or_10 (_5, and_15_out, and_17_out, and_16_out);
  or or_11 (_6, and_16_out, and_17_out);
endmodule
