// Logisim project logic test.circ as structural Verilog: 1 circuit, main circuit main
module main (
  input  A,
  input  B,
  output LED1,
  output LED2
);

  wire nand_1_out, nand_2_out, nand_3_out, nand_4_out, nand_5_out, nand_6_out, nand_7_out;

  nand nand_1 (nand_1_out, A, B);
  nand nand_2 (nand_2_out, A, A);
  nand nand_3 (nand_3_out, A, nand_1_out);
  nand nand_4 (nand_4_out, nand_1_out, B);
  nand nand_5 (nand_5_out, nand_2_out, B);
  nand nand_6 (nand_6_out, A, B);
  nand nand_7 (nand_7_out, nand_3_out, nand_4_out);
  nand nand_8 (LED2, nand_5_out, nand_6_out);
  nand nand_9 (LED1, nand_7_out, nand_7_out);
endmodule
